# Fritzing sketch Energy Monitor (saved by Fritzing 0.9.3b)
circuit board: 4.33127cm x 2.56554cm

parts:
  Composant1 = Arduino Nano (Rev3.0)
  R2 = Resistor [tolerance=±5% resistance=100k package=THT]
  R1 = Resistor [tolerance=±5% resistance=100k package=THT]
  R3 = Resistor [tolerance=±5% resistance=100k package=THT]
  R4 = Resistor [tolerance=±5% resistance=100k package=THT]
  C2 = Electrolytic Capacitor [capacitance=10µF package="100 mil [THT, electrolytic]"]
  SCT-013-30-1 = Inductor [package="400 mil [THT]"]
  SCT-013-30-2 = Inductor [package="400 mil [THT]"]
  C1 = Electrolytic Capacitor [capacitance=10µF voltage=6.3V package="100 mil [THT, electrolytic]"]
  NRF24L01+1 = NRF24L01+ Breakout Board
  C3 = Electrolytic Capacitor [capacitance=10µF package="100 mil [THT, electrolytic]"]

nets:
  GND: Composant1.GND, R2.Pin_0, R4.Pin_0, C2.-, C1.-, NRF24L01+1.GND, C3.-
  N1: Composant1.D2, NRF24L01+1.IRQ
  N2: Composant1.D9, NRF24L01+1.CE
  N3: Composant1.D10, NRF24L01+1.CS
  N4: Composant1.D11/MOSI, NRF24L01+1.MOSI
  N5: Composant1.D12/MISO, NRF24L01+1.MISO
  N6: Composant1.5V, R1.Pin_0, R3.Pin_0
  N7: Composant1.A1, SCT-013-30-2.pin_0
  N8: Composant1.A0, SCT-013-30-1.pin_0
  3V3: Composant1.3V3, NRF24L01+1.VCC, C3.+
  N9: Composant1.D13/SCK, NRF24L01+1.SCK
  N10: R2.Pin_1, R1.Pin_1, SCT-013-30-1.pin_1, C1.+
  N11: R3.Pin_1, R4.Pin_1, C2.+, SCT-013-30-2.pin_1
